# Fritzing sketch scheme (saved by Fritzing 0.9.3b)
breadboards: 1

parts:
  hc-sr1 = hc-sr04
  hc-sr2 = hc-sr04
  hc-sr3 = hc-sr04
  hc-sr5 = hc-sr04
  M1 = DC Motor  # not connected
  U5 = LIPO-2000mAh [package=lipo-2000]
  U6 = LIPO-2000mAh [package=lipo-2000]
  U7 = LIPO-2000mAh [package=lipo-2000]
  hc-sr6 = hc-sr04
  U8 = LIPO-2000mAh [package=lipo-2000]
  U9 = LIPO-2000mAh [package=lipo-2000]
  U10 = LIPO-2000mAh [package=lipo-2000]
  hc-sr7 = hc-sr04
  hc-sr8 = hc-sr04
  hc-sr9 = hc-sr04
  hc-sr10 = hc-sr04
  hc-sr11 = hc-sr04
  Part5 = Arduino Mega 2560 (Rev3)
  LM1 = RioRand LM2596
  M2 = BTS7960
  Raspberry_Pi_2 = Raspberry Pi 4 [part_number=RPI-4-b]  # not connected
  F1 = Fan - Ventilador [package=THT]
  LM2 = RioRand LM2596
  J1 = Basic Servo
  LM3 = RioRand LM2596
  GY1 = MPU-6050 Board GY-521 [form="♀ (female)" package=THT]

nets:
  VCC: hc-sr1.VCC, hc-sr2.VCC, hc-sr3.VCC, hc-sr5.VCC, hc-sr6.VCC, hc-sr7.VCC, hc-sr8.VCC, hc-sr9.VCC, hc-sr10.VCC, hc-sr11.VCC, LM2.Pin_2, GY1.pin1
  N1: hc-sr1.Trig, Part5.D23
  N2: hc-sr1.Echo, Part5.D22
  GND: hc-sr1.GND, hc-sr2.GND, hc-sr3.GND, hc-sr5.GND, hc-sr6.GND, hc-sr7.GND, hc-sr8.GND, hc-sr9.GND, hc-sr10.GND, hc-sr11.GND, LM2.Pin_3, GY1.pin2
  N3: hc-sr2.Trig, Part5.D3_PWM
  N4: hc-sr2.Echo, Part5.D2_PWM
  N5: hc-sr3.Trig, Part5.D13_PWM
  N6: hc-sr3.Echo, Part5.D12_PWM
  N7: hc-sr5.Trig, Part5.D25
  N8: hc-sr5.Echo, Part5.D24
  N9: U5.+, U7.-
  N10: U5.-, U6.+
  N11: U6.-, LM1.Pin_1
  N12: U7.+, LM1.Pin_0
  N13: hc-sr6.Trig, Part5.D29
  N14: hc-sr6.Echo, Part5.D28
  N15: U8.+, U10.-
  N16: U8.-, U9.+
  N17: U9.-, M2.pin12, LM2.Pin_1, LM3.Pin_1
  N18: U10.+, LM2.Pin_0
  N19: hc-sr7.Trig, Part5.D34
  N20: hc-sr7.Echo, Part5.D35
  N21: hc-sr8.Trig, Part5.D52
  N22: hc-sr8.Echo, Part5.D53
  N23: hc-sr9.Trig, Part5.D38
  N24: hc-sr9.Echo, Part5.D39
  N25: hc-sr10.Trig, Part5.D42
  N26: hc-sr10.Echo, Part5.D43
  N27: hc-sr11.Trig, Part5.D27
  N28: hc-sr11.Echo, Part5.D26
  N29: Part5.SCL, GY1.pin3
  N30: Part5.SDA, GY1.pin4
  N31: Part5.D11_PWM, M2.pin1
  N32: Part5.D10_PWM, M2.pin3
  N33: Part5.D9_PWM, M2.pin2
  N34: Part5.D8_PWM, M2.pin4
  N35: Part5.D7_PWM, J1.pulse
  N36: LM1.Pin_2, F1.5V
  N37: LM1.Pin_3, F1.GND
  N38: J1.gnd, LM3.Pin_3
  N39: J1.vcc, LM3.Pin_2

notes:
  R1
  R2
  L1
  L2
  F
  B
  D2L
  D2R
  BR
  BL
  12V Input - 5V Output

custom parts:
  BTS7960: BTS7960 43A Peak Power H-Bridge PWM Motor Driver
  Raspberry Pi 4: The RPi4, a faster version of the awesome Raspberry Pi 2 B ARM Board with 40 pin gpio. Ready for special Raspberry Pi B+ and RPi2 Hat (Hardware attached (on) top)
  Fan - Ventilador: Ventilador de 2 pines, se encuentra comunmente en computadoras de escritorio
  MPU-6050 Board GY-521: Acelerometro y Giroscopio MPU-6050 Board GY-521
